// Logisim project 273 Divider.circ as structural Verilog: 3 circuits, main circuit Divider
module Divider (
  input  [3:0] Dividend,
  input  [3:0] Divisor,
  input  RESET,
  output [3:0] Quotient,
  output [3:0] Remainder,
  output DONE
);

  wire CLK, CLK_out, INIT, noBORROW, not_2_out, s_r_ff_1_q, subtractor_1_bout;
  wire [3:0] subtractor_1_out;

  // Probe on Dividend
  // Probe on Divisor
  Clock u_CLK (.out(CLK_out));
  S_R_Flip_Flop s_r_ff_1 (.clk(1'b1), .Q(s_r_ff_1_q), .reset(RESET), .preset(DONE));  // open: S, R, Qn
  Subtractor #(.width(4)) subtractor_1 (
    .a(Remainder), .b(Divisor), .out(subtractor_1_out), .bout(subtractor_1_bout));  // open: bin
  not not_1 (noBORROW, subtractor_1_bout);
  and and_1 (CLK, CLK_out, not_2_out);
  not not_2 (not_2_out, s_r_ff_1_q);
  D_Flip_Flop d_ff_1 (.clk(CLK), .Q(INIT), .preset(CLK), .reset(RESET));  // open: D, Qn
  COUNT count_1 (.CLK(CLK), .RESET(RESET), .DONE(DONE));
  SHIFT shift_1 (
    .D({subtractor_1_out, Quotient}), .INIT(INIT), .R(RESET), .NOTNEG(noBORROW), .DONE(DONE), .CLK(CLK),
    .Dividend({4'b0000, Dividend}), .Q({Remainder, Quotient}));
  // Probe on Quotient
  // Probe on Remainder

  // Other names for the same wires on the sheet: Q[3:0] = Quotient; R = RESET

  // Notes on the sheet:
  //   Daphne HEGEDUS, 260762425
  //   Stops clock from affecting result once DONE
  //   Once clk ticks once, dividend has been loaded in to begin
endmodule

module COUNT (
  input  CLK,
  input  RESET,
  output DONE
);

  wire and_2_out, and_3_out, and_4_out, and_5_out, j_k_ff_1_q, j_k_ff_1_qn, j_k_ff_2_q, j_k_ff_2_qn,
       j_k_ff_3_q, not_1_out, not_2_out, or_1_out, or_2_out;

  and and_1 (DONE, j_k_ff_1_q, not_1_out, j_k_ff_3_q);
  not not_1 (not_1_out, j_k_ff_2_q);
  J_K_Flip_Flop j_k_ff_1 (
    .J(1'b1), .K(1'b1), .clk(CLK), .Q(j_k_ff_1_q), .Qn(j_k_ff_1_qn), .reset(RESET));  // open: preset
  // Probe on j_k_ff_1_q
  and and_2 (and_2_out, 1'b1, j_k_ff_1_q);
  and and_3 (and_3_out, j_k_ff_1_qn, not_2_out);
  not not_2 (not_2_out, 1'b1);
  J_K_Flip_Flop j_k_ff_2 (
    .J(or_1_out), .K(or_1_out), .clk(CLK), .Q(j_k_ff_2_q), .Qn(j_k_ff_2_qn), .reset(RESET));  // open: preset
  or or_1 (or_1_out, and_2_out, and_3_out);
  // Probe on j_k_ff_2_q
  and and_4 (and_4_out, and_2_out, j_k_ff_2_q);
  or or_2 (or_2_out, and_4_out, and_5_out);
  and and_5 (and_5_out, j_k_ff_2_qn, and_3_out);
  // Probe on j_k_ff_3_q
  J_K_Flip_Flop j_k_ff_3 (.J(or_2_out), .K(or_2_out), .clk(CLK), .Q(j_k_ff_3_q), .reset(RESET));  // open: Qn, preset

  // Notes on the sheet:
  //   Daphne HEGEDUS, 260762425
  //   stops after 5 ticks - 1 for init, 4 shifts
endmodule

module SHIFT (
  input  [7:0] D,
  input  INIT,
  input  R,
  input  NOTNEG,
  input  DONE,
  input  CLK,
  input  [7:0] Dividend,
  output [7:0] Q
);

  wire [7:0] multiplexer_1_out, multiplexer_2_out, register_1_q;

  Register register_1 (.D(multiplexer_1_out), .en(1'b1), .clk(CLK), .Q(register_1_q), .clr(R));
  Multiplexer #(.width(8), .enable("false")) multiplexer_1 (.in0(Q), .in1(D), .out(multiplexer_1_out), .sel(NOTNEG));
  Multiplexer #(.width(8), .enable("false")) multiplexer_2 (
    .in0({register_1_q[6:0], NOTNEG}), .in1(register_1_q), .out(multiplexer_2_out), .sel(DONE));
  Multiplexer #(.width(8), .enable("false")) multiplexer_3 (
    .in0(Dividend), .in1(multiplexer_2_out), .out(Q), .sel(INIT));

  // Notes on the sheet:
  //   Daphne HEGEDUS, 260762425
  //   if result from ALU is not negative -> takes new data
  //   Dividend is loaded in on first tick
endmodule
