// Logisim project 273 KITT.circ as structural Verilog: 2 circuits, main circuit KITT
module KITT (
  output [2:0] out_1
);

  wire updowncounter_1_tickout;
  wire [7:0] decoder_1_out0;

  Decoder #(.select(3), .tristate("true")) decoder_1 (
    .out0(decoder_1_out0[0]), .out1(decoder_1_out0[1]), .out2(decoder_1_out0[2]), .out3(decoder_1_out0[3]),
    .out4(decoder_1_out0[4]), .out5(decoder_1_out0[5]), .out6(decoder_1_out0[6]), .out7(decoder_1_out0[7]),
    .sel(out_1), .en(updowncounter_1_tickout));
  UpDownCounter updowncounter_1 (.A(out_1[0]), .B(out_1[1]), .C(out_1[2]), .tickout(updowncounter_1_tickout));
  LED led_1 (.in(decoder_1_out0[1]));
  LED led_2 (.in(decoder_1_out0[0]));
  LED led_3 (.in(decoder_1_out0[3]));
  LED led_4 (.in(decoder_1_out0[2]));
  LED led_5 (.in(decoder_1_out0[4]));
  LED led_6 (.in(decoder_1_out0[5]));
  LED led_7 (.in(decoder_1_out0[6]));
  LED led_8 (.in(decoder_1_out0[7]));

  // Notes on the sheet:
  //   Daphne HEGEDUS, 260762425
  //   run at 16 Hz after doing 1 reset simulation
endmodule

module UpDownCounter (
  output A,
  output B,
  output C,
  output tickout
);

  wire and_1_out, and_2_out, and_3_out, and_4_out, and_5_out, j_k_ff_1_qn, j_k_ff_2_qn, nor_1_out, not_1_out,
       or_1_out, or_2_out, s_r_ff_1_q;

  nor nor_1 (nor_1_out, C, B, A);
  and and_1 (and_1_out, A, B, C);
  S_R_Flip_Flop s_r_ff_1 (.Q(s_r_ff_1_q), .reset(and_1_out), .preset(nor_1_out));  // open: S, R, clk, Qn
  Clock tick (.out(tickout));
  J_K_Flip_Flop j_k_ff_1 (.J(1'b1), .K(1'b1), .clk(tickout), .Q(A), .Qn(j_k_ff_1_qn));  // open: preset, reset
  and and_2 (and_2_out, s_r_ff_1_q, A);
  and and_3 (and_3_out, j_k_ff_1_qn, not_1_out);
  not not_1 (not_1_out, s_r_ff_1_q);
  J_K_Flip_Flop j_k_ff_2 (.J(or_1_out), .K(or_1_out), .clk(tickout), .Q(B), .Qn(j_k_ff_2_qn));  // open: preset, reset
  or or_1 (or_1_out, and_2_out, and_3_out);
  and and_4 (and_4_out, and_2_out, B);
  or or_2 (or_2_out, and_4_out, and_5_out);
  and and_5 (and_5_out, j_k_ff_2_qn, and_3_out);
  J_K_Flip_Flop j_k_ff_3 (.J(or_2_out), .K(or_2_out), .clk(tickout), .Q(C));  // open: Qn, preset, reset

  // Notes on the sheet:
  //   Daphne HEGEDUS, 260762425 - 3 bit Up/Down Counter
endmodule
