// Logisim project 273 Multiplier.circ as structural Verilog: 3 circuits, main circuit Multiplier
module Multiplier (
  input  [3:0] A,
  input  [3:0] B,
  input  RESET,
  output [7:0] PRODUCT,
  output DONE
);

  wire CLK, CLK_out, cOut, INIT, not_1_out, s_r_ff_1_q;
  wire [3:0] adder_1_out;
  wire [7:0] multiplexer_1_out;

  // Probe on A
  // Probe on B
  Clock u_CLK (.out(CLK_out));
  S_R_Flip_Flop s_r_ff_1 (.clk(1'b1), .Q(s_r_ff_1_q), .reset(RESET), .preset(DONE));  // open: S, R, Qn
  Adder #(.width(4)) adder_1 (.a(PRODUCT[7:4]), .b(B), .out(adder_1_out), .cout(cOut));  // open: cin
  not not_1 (not_1_out, s_r_ff_1_q);
  and and_1 (CLK, CLK_out, not_1_out);
  Multiplexer #(.width(8), .enable("false")) multiplexer_1 (
    .in0({3'b000, A, 1'b0}), .in1({adder_1_out, PRODUCT[3:0]}), .out(multiplexer_1_out), .sel(PRODUCT[0]));
  D_Flip_Flop d_ff_1 (.clk(CLK), .Q(INIT), .preset(CLK), .reset(RESET));  // open: D, Qn
  COUNT count_1 (.CLK(CLK), .RESET(RESET), .DONE(DONE));
  // Probe on PRODUCT
  SHIFTright shiftright_1 (
    .D(multiplexer_1_out), .Initiated(INIT), .R(RESET), .LSB(PRODUCT[0]), .MSBin(cOut), .CLK(CLK), .Q(PRODUCT));

  // Other names for the same wires on the sheet: LSB = PRODUCT[0]; R = RESET

  // Notes on the sheet:
  //   Daphne HEGEDUS, 260762425
  //   loads A in shifted once to left (shifted >> w/ clk tick)
  //   Stops clock from affecting Product once DONE
  //   Once clk ticks once, A has been loaded into product to begin
endmodule

module SHIFTright (
  input  [7:0] D,
  input  Initiated,
  input  R,
  input  LSB,
  input  MSBin,
  input  CLK,
  output [7:0] Q
);

  wire d_ff_1_q, t_ff_1_q;
  wire [0:0] register_1_q;
  wire [7:0] multiplexer_1_out, multiplexer_2_out;

  Multiplexer #(.width(8), .enable("false")) multiplexer_1 (.in0(D), .in1(Q), .out(multiplexer_1_out), .sel(Initiated));
  Register register_1 (.D(multiplexer_2_out), .en(1'b1), .clk(CLK), .Q({Q[6:0], register_1_q[0]}), .clr(R));
  Multiplexer #(.width(8), .enable("false")) multiplexer_2 (
    .in0(multiplexer_1_out), .in1(D), .out(multiplexer_2_out), .sel(LSB));
  T_Flip_Flop t_ff_1 (.T(MSBin), .clk(CLK), .Q(t_ff_1_q), .reset(R));  // open: Qn, preset
  Multiplexer #(.enable("false")) multiplexer_3 (.in0(t_ff_1_q), .in1(d_ff_1_q), .out(Q[7]), .sel(register_1_q[0]));
  D_Flip_Flop d_ff_1 (.D(MSBin), .clk(CLK), .Q(d_ff_1_q), .reset(R));  // open: Qn, preset

  // Notes on the sheet:
  //   Daphne HEGEDUS, 260762425
  //   initiated becomes one once first load of a is done
  //   now takes from stored Q value (unless LSB is 1)
  //   if LSB is 1 it takes from D
endmodule

module COUNT (
  input  CLK,
  input  RESET,
  output DONE
);

  wire and_2_out, and_3_out, and_4_out, and_5_out, j_k_ff_1_q, j_k_ff_1_qn, j_k_ff_2_q, j_k_ff_2_qn,
       j_k_ff_3_q, not_1_out, not_2_out, or_1_out, or_2_out;

  and and_1 (DONE, j_k_ff_1_q, not_1_out, j_k_ff_3_q);
  not not_1 (not_1_out, j_k_ff_2_q);
  J_K_Flip_Flop j_k_ff_1 (
    .J(1'b1), .K(1'b1), .clk(CLK), .Q(j_k_ff_1_q), .Qn(j_k_ff_1_qn), .reset(RESET));  // open: preset
  // Probe on j_k_ff_1_q
  and and_2 (and_2_out, 1'b1, j_k_ff_1_q);
  and and_3 (and_3_out, j_k_ff_1_qn, not_2_out);
  not not_2 (not_2_out, 1'b1);
  J_K_Flip_Flop j_k_ff_2 (
    .J(or_1_out), .K(or_1_out), .clk(CLK), .Q(j_k_ff_2_q), .Qn(j_k_ff_2_qn), .reset(RESET));  // open: preset
  or or_1 (or_1_out, and_2_out, and_3_out);
  // Probe on j_k_ff_2_q
  and and_4 (and_4_out, and_2_out, j_k_ff_2_q);
  or or_2 (or_2_out, and_4_out, and_5_out);
  and and_5 (and_5_out, j_k_ff_2_qn, and_3_out);
  // Probe on j_k_ff_3_q
  J_K_Flip_Flop j_k_ff_3 (.J(or_2_out), .K(or_2_out), .clk(CLK), .Q(j_k_ff_3_q), .reset(RESET));  // open: Qn, preset

  // Notes on the sheet:
  //   Daphne HEGEDUS, 260762425
  //   stops after 5 ticks - 1 for init, 4 shifts
endmodule
