// Logisim project SevenSegDec.circ as structural Verilog: 2 circuits, main circuit SevenSegDec
module SevenSegDec (
  input  A3,
  input  A2,
  input  A1,
  input  A0,
  output S0,
  output S1,
  output S2,
  output S3,
  output S4,
  output S5,
  output S6
);

  wire pla_1_s0, pla_1_s1, pla_1_s2, pla_1_s3, pla_1_s4, pla_1_s5, pla_1_s6;

  PLA pla_1 (
    .A3(A3), .A2(A2), .A1(A1), .A0(A0), .s0(pla_1_s0), .s1(pla_1_s1), .s2(pla_1_s2), .s3(pla_1_s3),
    .s4(pla_1_s4), .s5(pla_1_s5), .s6(pla_1_s6));
  _7_Segment_Display u_7_segment_display_1 (
    .g(pla_1_s0), .f(pla_1_s1), .a(pla_1_s2), .b(pla_1_s3), .e(pla_1_s4), .d(pla_1_s5), .c(pla_1_s6));  // open: dp
  _7_Segment_Display u_7_segment_display_2 (.g(S0), .f(S1), .a(S2), .b(S3), .e(S4), .d(S5), .c(S6));  // open: dp

  // Notes on the sheet:
  //   Daphne Hegedus 260762425
endmodule

module PLA (
  input  A3,
  input  A2,
  input  A1,
  input  A0,
  output s0,
  output s1,
  output s2,
  output s3,
  output s4,
  output s5,
  output s6
);

  wire and_1_out, and_2_out, and_3_out, and_4_out, and_5_out, and_6_out, and_7_out, and_8_out, and_9_out,
       and_10_out, and_11_out, and_12_out, and_13_out, and_14_out, and_15_out, and_16_out, and_17_out,
       and_18_out, and_19_out, and_20_out, and_21_out, and_22_out, and_23_out, and_24_out, and_25_out,
       and_26_out, and_27_out, and_28_out, and_29_out, and_30_out, not_1_out, not_2_out, not_3_out,
       not_4_out, not_5_out, not_6_out, not_7_out, not_8_out, not_9_out, not_10_out, not_11_out, not_12_out,
       not_13_out, not_14_out, not_15_out, not_16_out, not_17_out, not_18_out, not_19_out, not_20_out,
       not_21_out, not_22_out, not_23_out, not_24_out, not_25_out, not_26_out, not_27_out, not_28_out,
       not_29_out, not_30_out, not_31_out, not_32_out, not_33_out, not_34_out, not_35_out, not_36_out,
       not_37_out, not_38_out, not_39_out, not_40_out, not_41_out, not_42_out;

  not not_1 (not_1_out, A3);
  and and_1 (and_1_out, not_1_out, not_2_out);
  not not_2 (not_2_out, A1);
  not not_3 (not_3_out, A3);
  and and_2 (and_2_out, not_3_out, A0);
  not not_4 (not_4_out, A3);
  and and_3 (and_3_out, not_4_out, not_5_out);
  not not_5 (not_5_out, A1);
  not not_6 (not_6_out, A2);
  and and_4 (and_4_out, not_6_out, not_7_out);
  not not_7 (not_7_out, A0);
  and and_5 (and_5_out, A2, A1);
  not not_8 (not_8_out, A3);
  and and_6 (and_6_out, not_8_out, not_9_out);
  not not_9 (not_9_out, A0);
  not not_10 (not_10_out, A2);
  and and_7 (and_7_out, not_10_out, A1, not_11_out);
  not not_11 (not_11_out, A0);
  and and_8 (and_8_out, A2, not_12_out);
  not not_12 (not_12_out, A1);
  and and_9 (and_9_out, A3, A2, A0);
  not not_13 (not_13_out, A3);
  not not_14 (not_14_out, A2);
  not not_15 (not_15_out, A1);
  not not_16 (not_16_out, A0);
  not not_17 (not_17_out, A2);
  not not_18 (not_18_out, A0);
  not not_19 (not_19_out, A2);
  not not_20 (not_20_out, A2);
  not not_21 (not_21_out, A1);
  not not_22 (not_22_out, A2);
  and and_10 (and_10_out, not_22_out, not_23_out);
  not not_23 (not_23_out, A1);
  not not_24 (not_24_out, A2);
  and and_11 (and_11_out, not_24_out, not_25_out);
  not not_25 (not_25_out, A0);
  not not_26 (not_26_out, A1);
  and and_12 (and_12_out, not_26_out, not_27_out);
  not not_27 (not_27_out, A0);
  not not_28 (not_28_out, A3);
  and and_13 (and_13_out, not_28_out, A0);
  not not_29 (not_29_out, A3);
  not not_30 (not_30_out, A2);
  and and_14 (and_14_out, not_29_out, not_30_out, A0);
  not not_31 (not_31_out, A2);
  and and_15 (and_15_out, not_31_out, not_32_out, A0);
  not not_32 (not_32_out, A1);
  not not_33 (not_33_out, A2);
  and and_16 (and_16_out, not_33_out, A1, not_34_out);
  not not_34 (not_34_out, A0);
  not not_35 (not_35_out, A3);
  and and_17 (and_17_out, not_35_out, A2, not_36_out);
  not not_36 (not_36_out, A0);
  and and_18 (and_18_out, A2, not_37_out, not_38_out);
  not not_37 (not_37_out, A1);
  not not_38 (not_38_out, A0);
  and and_19 (and_19_out, A3, A2, A0);
  not not_39 (not_39_out, A3);
  and and_20 (and_20_out, not_39_out, not_40_out, not_41_out);
  not not_40 (not_40_out, A2);
  not not_41 (not_41_out, A1);
  not not_42 (not_42_out, A2);
  and and_21 (and_21_out, not_42_out, A0);
  and and_22 (and_22_out, A2, A1);
  and and_23 (and_23_out, A3, A0);
  and and_24 (and_24_out, A3, A1);
  or or_1 (s0, and_1_out, and_2_out, A2);
  or or_2 (s1, and_3_out, and_4_out, and_5_out);
  or or_3 (s2, and_6_out, and_7_out, and_8_out, and_9_out);
  and and_25 (and_25_out, not_13_out, not_14_out, not_15_out, not_16_out);
  and and_26 (and_26_out, not_17_out, A1, A0);
  and and_27 (and_27_out, A2, A1, not_18_out);
  and and_28 (and_28_out, A3, not_19_out, A0);
  and and_29 (and_29_out, A3, not_20_out, A1);
  and and_30 (and_30_out, A3, A2, not_21_out);
  or or_4 (s4, and_10_out, and_11_out, and_12_out, and_13_out);
  or or_5 (s6, and_20_out, and_21_out, and_22_out, and_23_out, and_24_out);
  or or_6 (s3, and_25_out, and_26_out, and_27_out, and_28_out, and_29_out, and_30_out);
  or or_7 (s5, and_14_out, and_15_out, and_16_out, and_17_out, and_18_out, and_19_out);

  // Notes on the sheet:
  //   Daphne Hegedus, 260762425 (Subcircuit)
endmodule
